// Logisim project portas_logicas01.circ as structural Verilog: 1 circuit, main circuit main
module main (
  input  A,
  input  B,
  input  C,
  input  D,
  output out_5
);

  wire and_1_out, and_2_out;

  buf and_1 (and_1_out, A);  // AND_Gate
  and and_2 (and_2_out, C, D);
  or or_1 (out_5, and_1_out, and_2_out);
endmodule
